# Fritzing sketch FTDI_plug_in_v.0.1 (saved by Fritzing 0.9.0b)
circuit board: 2.58956cm x 1.20314cm
breadboards: 1

parts:
  U1 = Mystery Part - 12 pins [chip_label=? package=THT]
  U2 = Mystery Part - 12 pins [chip_label=? package=THT]
  X1 = USB Connectors [package=usb-a-pcb]
  R5 = Resistor [tolerance=±5% part_number="480 OHM" package="0402 [SMD]"]
  R6 = Resistor [tolerance=±5% part_number="480 OHM" package="0402 [SMD]"]
  Part2 = QFN-20-0.4MM [chip_label=FT230XQ package=QFN-20-0.4MM]
  R7 = Resistor [tolerance=±5% part_number="27 OHM" package="0402 [SMD]"]
  R8 = Resistor [tolerance=±5% part_number="27 OHM" package="0402 [SMD]"]
  C7 = Ceramic Capacitor 402 [capacitance=100nF part_number=.1uF package="0402 [SMD, multilayer]"]
  C9 = Ceramic Capacitor 402 [capacitance=100nF part_number=.1uF package="0402 [SMD, multilayer]"]
  C10 = Ceramic Capacitor 402 [capacitance=100nF part_number=10nF package="0402 [SMD, multilayer]"]
  C11 = Ceramic Capacitor 402 [capacitance=100nF part_number=47pF package="0402 [SMD, multilayer]"]
  C12 = Ceramic Capacitor 402 [capacitance=100nF part_number=47pF package="0402 [SMD, multilayer]"]
  LED4 = 0402 SMD LED [package=0402]
  LED3 = 0402 SMD LED [package=0402]
  C8 = Ceramic Capacitor 402 [part_number=4.7uF capacitance="100 nF" package="0402 [SMD, multilayer]"]

nets:
  DTR: U1.pin1, Part2.RTS#
  GND: U1.pin11, U2.pin11, X1.GND, Part2.GND, C7.0, C9.0, C10.0, C11.0, C12.0, LED4.anode, LED3.anode, C8.0
  5V: U1.pin12, X1.VBUS, Part2.VCC, C9.1, C10.1, C8.1
  TXD: U2.pin5, Part2.TXD
  RXD: U2.pin6, Part2.RXD
  N1: X1.D-, R7.Pin_1, C11.1
  N2: X1.D+, R8.Pin_1, C12.1
  N3: R5.Pin_0, Part2.CBUS2
  N4: R5.Pin_1, LED3.cathode
  N5: R6.Pin_0, Part2.CBUS1
  N6: R6.Pin_1, LED4.cathode
  decap: Part2.VCCIO, Part2.3V3OUT, Part2.RESET#, C7.1
  N7: Part2.USBDP, R8.Pin_0
  N8: Part2.USBDM, R7.Pin_0

notes:
  DTR
  6
  7
  9
  5
  2
  4
  3
  RST
  A5
  ~
  12
  11
  10
  13
  8
  A3
  A4
  GND
  VCC
  1
  VIN
  0
  USBDP (D+)
  USBDM (D-)
  USB

custom parts:
  Mystery Part - 12 pins: A dummy, proxy, ersatz, stand-in part for whatever you want. With 12 pins on a 100 mil inline pin header footprint.
  Resistor: Resistor Basic schematic elements and footprints for 0603, 1206, and PTH resistors.
  Ceramic Capacitor 402: 0.01 nF multilayered Ceramic Capacitor
  0402 SMD LED: Blue 0402 SMD LED
