# Fritzing sketch shield - FreeIMU  v.0.1 (saved by Fritzing 0.9.0b)
circuit board: 1.66cm x 1.16cm
breadboards: 1

parts:
  U1 = Mystery Part - 12 pins [chip_label=? package=THT]
  U2 = Mystery Part - 12 pins [chip_label=? package=THT]
  U3 = HMC5883L [package=16lpcc]  # not connected
  IC1 = QFN-24 [chip_label=MPU6050 package=QFN]
  U4 = Voltage Regulator LDO [package=sot23-5]
  C1 = Ceramic Capacitor 402 [part_number=2.2uF package="0402 [SMD, multilayer]"]
  C2 = Ceramic Capacitor 402 [part_number=2.2uF package="0402 [SMD, multilayer]"]
  C3 = Ceramic Capacitor 402 [part_number=2.2nF package="0402 [SMD, multilayer]"]
  C4 = Ceramic Capacitor 402 [part_number=0.1uF package="0402 [SMD, multilayer]"]
  C5 = Ceramic Capacitor 402 [part_number=0.1uF package="0402 [SMD, multilayer]"]
  C6 = Ceramic Capacitor 402 [part_number=10nF package="0402 [SMD, multilayer]"]
  R3 = Resistor [part_number="4.7K ohm" package="0402 [SMD]"]
  R4 = Resistor [part_number="4.7K ohm" package="0402 [SMD]"]
  Pad1 = Pad [width=2.3 height=2.3 connect=center]  # not connected

nets:
  GND: U1.pin11, U2.pin11, IC1.9, IC1.18, U4.GND, C1.0, C2.0, C3.1, C4.0, C5.0, C6.0
  SDA: U2.pin2, IC1.24, R3.Pin_1
  SCL: U2.pin3, IC1.23, R4.Pin_1
  VIN: U2.pin12, U4.IN, U4.EN, C2.1
  A_SDA: IC1.6
  A_SCL: IC1.7
  3.3V: IC1.8, IC1.13, U4.OUT, C1.1, C4.1, C6.1, R3.Pin_0, R4.Pin_0
  N1: IC1.10, C5.1
  FSYNC: IC1.11
  INTA: IC1.12
  N2: IC1.20, C3.0

notes:
  DTR
  6
  7
  9
  5
  2
  4
  3
  RST
  A5
  ~
  12
  11
  10
  13
  8
  A3
  A4
  GND
  5V
  1
  VIN
  VCC
  0
  MicroBit
  IMU shield V.0.1
  328

custom parts:
  Mystery Part - 12 pins: A dummy, proxy, ersatz, stand-in part for whatever you want. With 12 pins on a 100 mil inline pin header footprint.
  Ceramic Capacitor 402: 0.01 nF multilayered Ceramic Capacitor
  Resistor: Resistor Basic schematic elements and footprints for 0603, 1206, and PTH resistors.
