# Fritzing sketch shield - I2C pull up v.0.1 (saved by Fritzing 0.9.0b)
circuit board: 1.66cm x 1.16cm
breadboards: 1

parts:
  U1 = Mystery Part - 12 pins [chip_label=? package=THT]  # not connected
  U2 = Mystery Part - 12 pins [chip_label=? package=THT]
  R1 = Resistor [tolerance=±5% resistance=4.7k package="0603 [SMD]"]
  R2 = Resistor [tolerance=±5% resistance=4.7k package="0603 [SMD]"]

nets:
  N1: U2.pin2, R1.Pin_0
  N2: U2.pin3, R2.Pin_0
  5V: U2.pin10, R1.Pin_1, R2.Pin_1

notes:
  DTR
  6
  7
  9
  5
  2
  4
  3
  RST
  A5
  ~
  12
  11
  10
  13
  8
  A3
  A4
  GND
  VCC
  1
  VIN
  0
  for MicroBit 328
  I2C pull up Shield

custom parts:
  Mystery Part - 12 pins: A dummy, proxy, ersatz, stand-in part for whatever you want. With 12 pins on a 100 mil inline pin header footprint.
