# Fritzing sketch shield - RGB LED  v.0.1 (saved by Fritzing 0.9.0b)
circuit board: 1.66cm x 1.16cm
breadboards: 1

parts:
  U1 = Mystery Part - 12 pins [chip_label=? package=THT]
  U2 = Mystery Part - 12 pins [chip_label=? package=THT]
  LED1 = RGB LED SMD [package=SMD]
  LED2 = RGB LED SMD [package=SMD]
  R2 = Resistor [package="0402 [SMD]"]
  R3 = Resistor [package="0402 [SMD]"]
  R4 = Resistor [package="0402 [SMD]"]
  R5 = Resistor [package="0402 [SMD]"]
  R6 = Resistor [package="0402 [SMD]"]
  R7 = Resistor [package="0402 [SMD]"]

nets:
  N1: U1.pin4, R5.Pin_0
  N2: U1.pin5, R6.Pin_0
  N3: U1.pin6, R7.Pin_0
  N4: U1.pin9, R3.Pin_0
  N5: U1.pin10, R4.Pin_0
  N6: U2.pin8, R2.Pin_1
  N7: U2.pin12, LED1.common_cathode, LED2.common_cathode
  N8: LED1.red_anode, R6.Pin_1
  N9: LED1.green_anode, R5.Pin_1
  N10: LED1.blue_anode, R7.Pin_1
  N11: LED2.red_anode, R3.Pin_1
  N12: LED2.green_anode, R2.Pin_0
  N13: LED2.blue_anode, R4.Pin_1

notes:
  DTR
  6
  7
  9
  5
  2
  4
  3
  RST
  A5
  ~
  12
  11
  10
  13
  8
  A3
  A4
  GND
  5V
  1
  VIN
  VCC
  0

custom parts:
  Mystery Part - 12 pins: A dummy, proxy, ersatz, stand-in part for whatever you want. With 12 pins on a 100 mil inline pin header footprint.
  RGB LED SMD: SMD RGB LED
  Resistor: Resistor Basic schematic elements and footprints for 0603, 1206, and PTH resistors.
