# Fritzing sketch breakout board microbit328 (saved by Fritzing 0.9.0b)
circuit board: 3.07cm x 1.6cm
breadboards: 1

parts:
  U1 = Mystery Part - 12 pins [chip_label=? package=THT]
  U2 = Mystery Part - 12 pins [chip_label=? package=THT]
  U3 = mystery part, 12 pins [chip_label=?]
  U4 = mystery part, 12 pins [chip_label=?]

nets:
  N1: U1.pin1, U3.pin12
  N2: U1.pin2, U3.pin11
  N3: U1.pin3, U3.pin10
  N4: U1.pin4, U3.pin9
  N5: U1.pin5, U3.pin8
  N6: U1.pin6, U3.pin7
  N7: U1.pin7, U3.pin6
  N8: U1.pin8, U3.pin5
  N9: U1.pin9, U3.pin4
  N10: U1.pin10, U3.pin3
  N11: U1.pin11, U3.pin2
  N12: U1.pin12, U3.pin1
  N13: U2.pin1, U4.pin12
  N14: U2.pin2, U4.pin11
  N15: U2.pin3, U4.pin10
  N16: U2.pin4, U4.pin9
  N17: U2.pin5, U4.pin8
  N18: U2.pin6, U4.pin7
  N19: U2.pin7, U4.pin6
  N20: U2.pin8, U4.pin5
  N21: U2.pin9, U4.pin4
  N22: U2.pin10, U4.pin3
  N23: U2.pin11, U4.pin2
  N24: U2.pin12, U4.pin1

notes:
  DTR
  6
  7
  9
  5
  2
  4
  3
  RST
  A5
  ~
  12
  11
  10
  13
  8
  A3
  A4
  GND
  VCC
  1
  VIN
  0
  MicroBit 328

custom parts:
  Mystery Part - 12 pins: A dummy, proxy, ersatz, stand-in part for whatever you want. With 12 pins on a 100 mil inline pin header footprint.
