# Fritzing sketch I2C pull up module (saved by Fritzing 0.9.0b)
circuit board: 0.635cm x 0.807829cm
breadboards: 1

parts:
  4_pin_header1 = 4 pin 1.27mm [chip_label=header package=THT]
  4_pin_header2 = 4 pin 1.27mm [chip_label=header package=THT]
  R1 = Resistor [tolerance=±5% resistance=220 package="0603 [SMD]"]
  R2 = Resistor [tolerance=±5% resistance=220 package="0603 [SMD]"]

nets:
  N1: 4_pin_header1.pin1, 4_pin_header2.pin1, R2.Pin_0
  N2: 4_pin_header1.pin2, 4_pin_header2.pin2, R1.Pin_0
  N3: 4_pin_header1.pin3, 4_pin_header2.pin3
  N4: 4_pin_header1.pin4, 4_pin_header2.pin4, R1.Pin_1, R2.Pin_1

notes:
  A4
  A5
  GND
  5V

custom parts:
  4 pin 1.27mm: tested footprint for 1.27mm 4 pin
