# Fritzing sketch Servo_shield_v.0.1 (saved by Fritzing 0.9.0b)
circuit board: 1.66cm x 1.16cm
breadboards: 1

parts:
  U1 = Mystery Part - 12 pins [chip_label=? package=THT]
  U2 = Mystery Part - 12 pins [chip_label=? package=THT]
  servo1 = mystery part, 3 pins [chip_label=?]
  servo2 = mystery part, 3 pins [chip_label=?]
  Power = mystery part, 2 pins [chip_label=?]

nets:
  s2: U1.pin9, servo2.pin3
  s1: U1.pin10, servo1.pin3
  GND: U1.pin11, U2.pin11, servo1.pin1, servo2.pin1, Power.pin1
  VIN: U1.pin12, U2.pin12, servo1.pin2, servo2.pin2, Power.pin2

notes:
  DTR
  6
  7
  9
  5
  2
  4
  3
  RST
  A5
  ~
  12
  11
  10
  13
  8
  A3
  A4
  GND
  VIN
  1
  VCC
  0
  S1
  S2
  +
  -
  D

custom parts:
  Mystery Part - 12 pins: A dummy, proxy, ersatz, stand-in part for whatever you want. With 12 pins on a 100 mil inline pin header footprint.
