# Fritzing sketch MicroBit V.0.2 (saved by Fritzing 0.9.0b)
circuit board: 1.66452cm x 1.16cm
breadboards: 1

parts:
  Part1 = QFN-28 [package=QFN-28]
  U1 = Voltage Regulator LDO [package=sot23-5]
  Y1 = Resonator [package=resonator-smd]
  C1 = Ceramic Capacitor 402 [part_number=0.1uf package="0402 [SMD, multilayer]"]
  C4 = Ceramic Capacitor 402 [part_number=0.1uf package="0402 [SMD, multilayer]"]
  C3 = Ceramic Capacitor 402 [capacitance=4.7µF voltage=20V part_number=2.2uf package="0402 [SMD, multilayer]"]
  C2 = Ceramic Capacitor 402 [capacitance=4.7µF voltage=20V part_number=2.2uf package="0402 [SMD, multilayer]"]
  U3 = Mystery Part - 12 pins [chip_label=? package=THT]
  U4 = Mystery Part - 12 pins [chip_label=? package=THT]
  R1 = Resistor [part_number="470 ohm" package="0402 [SMD]"]
  C5 = Ceramic Capacitor 402 [capacitance=100nF part_number=0.1uf package="0402 [SMD, multilayer]"]
  C6 = Ceramic Capacitor 402 [capacitance=100nF part_number=0.1uf package="0402 [SMD, multilayer]"]
  LED1 = Blue smd LED [package="0603 [SMD]"]
  Pad1 = Pad [width=0.5 height=0.5 connect=center]  # not connected
  Pad2 = Pad [width=0.5 height=0.5 connect=center]  # not connected
  Header1 = 6 pin SMD 1.27mm header [package=SMD]

nets:
  D3: Part1.PD3, U4.pin8
  D4: Part1.PD4, U4.pin9
  5V: Part1.VCC, Part1.AVCC, U1.OUT, C1.1, C3.1, U3.pin12, U4.pin10, R1.Pin_0, C6.1, Header1.DTR
  GND: Part1.GND, Part1.pin_28, U1.GND, Y1.2, C1.0, C4.0, C3.0, C2.0, U3.pin11, U4.pin11, C6.0, LED1.anode, Header1.GND#2, Header1.TX
  N1: Part1.PB6, Y1.1
  N2: Part1.PB7, Y1.3
  D5: Part1.PD5, U3.pin10
  D6: Part1.PD6, U3.pin9
  D7: Part1.PD7, U3.pin8
  D8: Part1.PB0, U3.pin7
  D9: Part1.PB1, U3.pin6
  D10: Part1.PB2, U3.pin5
  D11: Part1.PB3, U3.pin4
  D12: Part1.PB4, U3.pin3
  D13: Part1.PB5, U3.pin2
  N3: Part1.AREF, C4.1
  A3: Part1.PC3, U4.pin1
  A4: Part1.PC4, U4.pin2
  A5: Part1.PC5, U4.pin3
  rst: Part1.PC6, U4.pin4, C5.0
  D0: Part1.PD0, U4.pin5, Header1.GND#5
  D1: Part1.PD1, U4.pin6, Header1.RX
  D2: Part1.PD2, U4.pin7
  VCC: U1.IN, U1.EN, C2.1, U4.pin12
  DTR: U3.pin1, C5.1, Header1.5V
  N4: R1.Pin_1, LED1.cathode

notes:
  V reg, same circuit for voltages 1.8v to 5v, 0.1
  PWR
  GND
  VIN
  0
  1
  5V
  A4
  A3
  8
  13
  10
  11
  12
  A2
  Version 0.2
  MicroBit 328
  5.0V
  3.3V
  1.8V
  RST
  VCC
  3
  4
  2
  A5
  9
  5
  7
  6
  DTR
  ~

custom parts:
  QFN-28: Atmega328P - 28QFN 4mm body
  Ceramic Capacitor 402: 0.01 nF multilayered Ceramic Capacitor
  Mystery Part - 12 pins: A dummy, proxy, ersatz, stand-in part for whatever you want. With 12 pins on a 100 mil inline pin header footprint.
  Resistor: Resistor Basic schematic elements and footprints for 0603, 1206, and PTH resistors.
  Blue smd LED: A generic blue LED (~1.8V)
