# Fritzing sketch MicroBit V.0.5 - remake (saved by Fritzing 0.9.0b)
circuit board: 1.66452cm x 1.16cm
breadboards: 1

parts:
  U1 = Voltage Regulator LDO [package=sot23-5]
  Y1 = Resonator [package=resonator-smd]
  C1 = Ceramic Capacitor 402 [part_number=0.1uf package="0402 [SMD, multilayer]"]
  C4 = Ceramic Capacitor 402 [part_number=0.1uf package="0402 [SMD, multilayer]"]
  C3 = Ceramic Capacitor 402 [capacitance=4.7µF voltage=20V part_number=2.2uf package="0402 [SMD, multilayer]"]
  C2 = Ceramic Capacitor 402 [capacitance=4.7µF voltage=20V part_number=2.2uf package="0402 [SMD, multilayer]"]
  U3 = Mystery Part - 12 pins [chip_label=? package=THT]
  U4 = Mystery Part - 12 pins [chip_label=? package=THT]
  C5 = Ceramic Capacitor 402 [capacitance=100nF part_number=0.1uf package="0402 [SMD, multilayer]"]
  C6 = Ceramic Capacitor 402 [capacitance=100nF part_number=0.1uf package="0402 [SMD, multilayer]"]
  Header1 = 6 pin SMD 1.27mm header [package=SMD]
  Part1 = QFN-28 [package=QFN-28]
  R2 = Resistor [package="0402 [SMD]"]
  LED2 = 0402 SMD LED [package=0402]
  R3 = Resistor [part_number=10K package="0402 [SMD]"]

nets:
  VCC: U1.IN, U1.EN, C2.1, U4.pin12
  GND: U1.GND, Y1.2, C1.0, C4.0, C3.0, C2.0, U3.pin11, U4.pin11, C6.0, Header1.GND#2, Header1.TX, Part1.GND, Part1.pin_28, R2.Pin_0
  5V: U1.OUT, C1.1, C3.1, U3.pin12, U4.pin10, C6.1, Header1.DTR, Part1.VCC, Part1.AVCC, LED2.cathode, R3.Pin_0
  N1: Y1.1, Part1.PB6
  N2: Y1.3, Part1.PB7
  N3: C4.1, Part1.AREF
  DTR: U3.pin1, C5.1, Header1.5V
  D13: U3.pin2, Part1.PB5
  D12: U3.pin3, Part1.PB4
  D11: U3.pin4, Part1.PB3
  D10: U3.pin5, Part1.PB2
  D9: U3.pin6, Part1.PB1
  D8: U3.pin7, Part1.PB0
  D7: U3.pin8, Part1.PD7
  D6: U3.pin9, Part1.PD6
  D5: U3.pin10, Part1.PD5
  A3: U4.pin1, Part1.PC3
  A4: U4.pin2, Part1.PC4
  A5: U4.pin3, Part1.PC5
  rst: U4.pin4, C5.0, Part1.PC6, R3.Pin_1
  D0: U4.pin5, Header1.GND#5, Part1.PD0
  D1: U4.pin6, Header1.RX, Part1.PD1
  D2: U4.pin7, Part1.PD2
  D3: U4.pin8, Part1.PD3
  D4: U4.pin9, Part1.PD4
  N4: R2.Pin_1, LED2.anode

notes:
  V reg, same circuit for voltages 1.8v to 5v, 0.1
  PWR
  GND
  VIN
  0
  1
  5V
  A4
  A3
  8
  13
  10
  11
  12
  A2
  v0.5
  MicroBit 328
  5.0V
  3.3V
  1.8V
  RST
  VCC
  3
  4
  2
  A5
  9
  5
  7
  6
  DTR
  ~

custom parts:
  Ceramic Capacitor 402: 0.01 nF multilayered Ceramic Capacitor
  Mystery Part - 12 pins: A dummy, proxy, ersatz, stand-in part for whatever you want. With 12 pins on a 100 mil inline pin header footprint.
  QFN-28: Atmega328P - 28QFN 4mm body FIXED
  Resistor: Resistor Basic schematic elements and footprints for 0603, 1206, and PTH resistors.
  0402 SMD LED: Blue 0402 SMD LED
